# Fritzing sketch SpyTag-Wifi-game (saved by Fritzing 0.9.3b)

parts:
  U1 = ESP8266 WiFi Module [part_number=ESP8266]
  Part1 = ws2812b [package="smd 2812b"]
  S1 = Pushbutton [package="[SMD]"]
  S2 = Pushbutton [package="[SMD]"]
  Part2 = ws2812b [package="smd 2812b"]
  S3 = Toggle Switch [package=THT]
  U2 = BATTERY-2 [package=battery-aaa]
  U3 = BATTERY-2 [package=battery-aaa]

nets:
  N1: U1.IO0, S1.Pin_1, S1.Pin_2
  N2: U1.IO2, Part1.DIN
  VDD: U1.3.3V, U1.CHIP_EN, Part1.VDD, Part2.VDD, S3.COM
  VSS: U1.GND, U1.IO15, Part1.VSS, S1.Pin_3, S1.Pin_4, S2.Pin_1, S2.Pin_2, Part2.VSS, U3.-1
  N3: U1.IO12, S2.Pin_3, S2.Pin_4
  N4: Part1.DOUT, Part2.DIN
  N5: S3.L2, U2.+1
  N6: U2.-1, U3.+1

notes:
  IO 2
  IO 0
  3.3 V
  IO 15
  IO 12
  CH_EN
  GND
